// Logisim project CARRYLOOKAHEAD.circ as structural Verilog: 1 circuit, main circuit main
module main (
  input  C0,
  input  X0,
  input  X1,
  input  X2,
  input  X3,
  input  Y0,
  input  Y1,
  input  Y2,
  input  Y3,
  output su0,
  output su1,
  output su2,
  output su3,
  output ca4
);

  wire and_1_out, and_2_out, and_3_out, and_4_out, and_5_out, and_6_out, and_7_out, and_8_out, and_9_out,
       and_10_out, and_11_out, and_12_out, C1_out, C2_out, C3_out, G0_out, G1_out, G2_out, G3_out, or_1_out,
       or_2_out, or_3_out, or_4_out, or_5_out, or_6_out, P0_out, P0C0_out, P1_out, P1C1_out, P2_out,
       P2C2_out, P3_out, P3C3_out, xor_1_out, xor_2_out, xor_3_out, xor_4_out, xor_5_out, xor_6_out,
       xor_7_out, xor_9_out, xor_11_out, xor_13_out;

  xor P2 (P2_out, X2, Y2);
  and G2 (G2_out, X2, Y2);
  xor xor_1 (xor_1_out, X2, Y2);
  and and_1 (and_1_out, X2, Y2);
  xor P3 (P3_out, X3, Y3);
  and G3 (G3_out, X3, Y3);
  xor xor_2 (xor_2_out, X0, Y0);
  xor P1 (P1_out, X1, Y1);
  and G1 (G1_out, X1, Y1);
  and and_2 (and_2_out, X1, Y1);
  and and_3 (and_3_out, X1, Y1);
  xor P0 (P0_out, X0, Y0);
  and G0 (G0_out, X0, Y0);
  and and_4 (and_4_out, X0, Y0);
  xor xor_3 (xor_3_out, X0, Y0);
  and and_5 (and_5_out, X0, Y0);
  xor xor_4 (xor_4_out, X1, Y1);
  xor xor_5 (xor_5_out, X0, Y0);
  and and_6 (and_6_out, X0, Y0);
  xor xor_6 (xor_6_out, X1, Y1);
  and and_7 (and_7_out, C0, xor_2_out);
  and and_8 (and_8_out, C0, xor_3_out);
  and and_9 (and_9_out, C0, xor_5_out);
  and P0C0 (P0C0_out, C0, P0_out);
  or or_1 (or_1_out, and_7_out, and_4_out);
  or C1 (C1_out, P0C0_out, G0_out);
  or or_2 (or_2_out, and_8_out, and_5_out);
  or or_3 (or_3_out, and_9_out, and_6_out);
  and P1C1 (P1C1_out, or_1_out, P1_out);
  and and_10 (and_10_out, or_2_out, xor_4_out);
  and and_11 (and_11_out, or_3_out, xor_6_out);
  or C2 (C2_out, P1C1_out, G1_out);
  or or_4 (or_4_out, and_10_out, and_2_out);
  or or_5 (or_5_out, and_11_out, and_3_out);
  xor xor_7 (xor_7_out, C0, X0);
  xor xor_8 (su0, xor_7_out, Y0);
  xor xor_9 (xor_9_out, C1_out, X1);
  xor xor_10 (su1, xor_9_out, Y1);
  xor xor_11 (xor_11_out, C2_out, X2);
  and P2C2 (P2C2_out, or_4_out, P2_out);
  and and_12 (and_12_out, or_5_out, xor_1_out);
  xor xor_12 (su2, xor_11_out, Y2);
  or C3 (C3_out, P2C2_out, G2_out);
  or or_6 (or_6_out, and_12_out, and_1_out);
  and P3C3 (P3C3_out, or_6_out, P3_out);
  xor xor_13 (xor_13_out, C3_out, X3);
  xor xor_14 (su3, xor_13_out, Y3);
  or C4 (ca4, P3C3_out, G3_out);
endmodule
