// Logisim project univ.circ as structural Verilog: 1 circuit, main circuit main
module main (
  input  I0,
  input  I1,
  input  I2,
  input  I3,
  input  D,
  input  [1:0] S,
  input  SET,
  input  R,
  input  in_9,
  input  in_10,
  input  in_11,
  input  in_12,
  input  in_13
);

  wire CLK_out, clock_1_out, d_ff_1_q, d_ff_2_q, d_ff_3_q, d_ff_4_q, d_ff_5_q, d_ff_6_q, d_ff_7_q, d_ff_8_q,
       multiplexer_1_out, multiplexer_2_out, multiplexer_3_out, multiplexer_4_out, multiplexer_5_out,
       multiplexer_6_out, multiplexer_7_out, multiplexer_8_out;

  Clock CLK (.out(CLK_out));
  Clock clock_1 (.out(clock_1_out));
  Multiplexer #(.select(2)) multiplexer_1 (
    .in0(D), .in1(d_ff_3_q), .in2(I0), .in3(d_ff_1_q), .out(multiplexer_1_out), .sel(S));
  D_Flip_Flop d_ff_1 (.D(multiplexer_1_out), .clk(CLK_out), .Q(d_ff_1_q), .preset(SET), .reset(R));  // open: Qn
  Multiplexer multiplexer_2 (.in0(in_10), .in1(d_ff_4_q), .out(multiplexer_2_out), .sel(in_11));
  D_Flip_Flop d_ff_2 (
    .D(multiplexer_2_out), .clk(clock_1_out), .Q(d_ff_2_q), .preset(in_12), .reset(in_13));  // open: Qn
  D_Flip_Flop d_ff_3 (.D(multiplexer_3_out), .clk(CLK_out), .Q(d_ff_3_q), .preset(SET), .reset(R));  // open: Qn
  LED led_1 (.in(d_ff_1_q));
  LED led_2 (.in(d_ff_2_q));
  Multiplexer #(.select(2)) multiplexer_3 (
    .in0(d_ff_1_q), .in1(d_ff_5_q), .in2(I1), .in3(d_ff_3_q), .out(multiplexer_3_out), .sel(S));
  LED led_3 (.in(d_ff_3_q));
  Multiplexer multiplexer_4 (.in0(d_ff_2_q), .in1(d_ff_6_q), .out(multiplexer_4_out), .sel(in_11));
  D_Flip_Flop d_ff_4 (
    .D(multiplexer_4_out), .clk(clock_1_out), .Q(d_ff_4_q), .preset(in_12), .reset(in_13));  // open: Qn
  Multiplexer #(.select(2)) multiplexer_5 (
    .in0(d_ff_3_q), .in1(d_ff_7_q), .in2(I2), .in3(d_ff_5_q), .out(multiplexer_5_out), .sel(S));
  D_Flip_Flop d_ff_5 (.D(multiplexer_5_out), .clk(CLK_out), .Q(d_ff_5_q), .preset(SET), .reset(R));  // open: Qn
  D_Flip_Flop d_ff_6 (
    .D(multiplexer_6_out), .clk(clock_1_out), .Q(d_ff_6_q), .preset(in_12), .reset(in_13));  // open: Qn
  LED led_4 (.in(d_ff_4_q));
  LED led_5 (.in(d_ff_5_q));
  Multiplexer multiplexer_6 (.in0(d_ff_4_q), .in1(d_ff_8_q), .out(multiplexer_6_out), .sel(in_11));
  LED led_6 (.in(d_ff_6_q));
  Multiplexer #(.select(2)) multiplexer_7 (
    .in0(d_ff_5_q), .in1(D), .in2(I3), .in3(d_ff_7_q), .out(multiplexer_7_out), .sel(S));
  D_Flip_Flop d_ff_7 (.D(multiplexer_7_out), .clk(CLK_out), .Q(d_ff_7_q), .preset(SET), .reset(R));  // open: Qn
  Multiplexer multiplexer_8 (.in0(d_ff_6_q), .in1(in_9), .out(multiplexer_8_out), .sel(in_11));
  D_Flip_Flop d_ff_8 (
    .D(multiplexer_8_out), .clk(clock_1_out), .Q(d_ff_8_q), .preset(in_12), .reset(in_13));  // open: Qn
  LED led_7 (.in(d_ff_7_q));
  LED led_8 (.in(d_ff_8_q));
endmodule
